# Fritzing sketch RemoteControlCar (saved by Fritzing 0.9.3b)

parts:
  Raspberry_Pi_1 = Raspberry Pi 3 [part_number=RPI-3-V1.2]
  S1 = H-Bridge with L298N
  M1 = DC Motor
  M2 = DC Motor
  M3 = DC Motor
  M4 = DC Motor
  VCC1 = Battery
  VCC2 = Battery

nets:
  N1: Raspberry_Pi_1.GIPO13, S1.ENB
  N2: Raspberry_Pi_1.GIPO19, S1.IN4
  N3: Raspberry_Pi_1.GIPO26, S1.IN3
  N4: Raspberry_Pi_1.GIPO21, S1.ENA
  N5: Raspberry_Pi_1.GIPO20, S1.IN1
  N6: Raspberry_Pi_1.GIPO16, S1.IN2
  GND: Raspberry_Pi_1.GND, S1.GND, VCC1.-, VCC2.-
  5V: Raspberry_Pi_1.5V, S1.5V
  N7: S1.12V, VCC1.+, VCC2.+
  N8: S1.M1-01, M3.pin_2, M4.pin_2
  N9: S1.M1-02, M3.pin_1, M4.pin_1
  N10: S1.M2-01, M1.pin_2, M2.pin_2
  N11: S1.M2-02, M1.pin_1, M2.pin_1

notes:
  神火 18650 强光手电专用锂电池
  Li-ion 18650 1700mAh 3.7V-A * 2

custom parts:
  H-Bridge with L298N: h-bridge
